# Fritzing sketch circuit-diagram (saved by Fritzing 0.9.3b)
breadboards: 1

parts:
  U1 = NodeMCU V3.0
  U2 = NodeMCU V3.0
  R1 = Resistor [tolerance=±5% resistance=4.7k package="0805 [SMD]"]
  GY-NEO6MV3 = SUP500F [package=sup500f]

nets:
  N1: U1.D1, GY-NEO6MV3.RX-I
  N2: U1.D2, GY-NEO6MV3.TX-O
  N3: U1.D3, U2.D1, R1.Pin_0
  3V3: U1.3V3, GY-NEO6MV3.VCC
  N4: U1.GND#6, U1.GND#13, U1.GND#16, U1.GND#33, GY-NEO6MV3.GND
  N5: U2.GND#6, U2.GND#13, U2.GND#16, U2.GND#33, R1.Pin_1

custom parts:
  NodeMCU V3.0: ESP8266 based NodeMCU
